// Digital circuit 8 bit procssor.dig as structural Verilog
module _8_bit_procssor (
  input  [7:0] InstrMem_input,
  input  [1:0] InstrMem_ctrl,
  input  clk,
  output [2:0] Program_Counter,
  output [7:0] IR_output,
  output [1:0] IR_ctrl,
  output Inst_Fetch,
  output Inst_Decode,
  output Inst_Exec,
  output Write_Back,
  output [7:0] RegFile_ctrl,
  output [7:0] ALU_output
);

  wire and_1_out, not_1_out, not_2_out;
  wire [7:0] multiplexer_1_out, multiplexer_3_out, register_file_4x8_2r1w_1_rd1,
       register_file_4x8_2r1w_1_rd2, sram_1_p8;
  wire [7:3] pc8_1_pc;

  PC8 pc8_1 (.INC(Write_Back), .LD(1'b0), .Val({8{1'b0}}), .RST(1'b0), .CLK(clk), .PC({pc8_1_pc, Program_Counter}));
  not not_1 (not_1_out, InstrMem_ctrl[1]);
  and and_1 (and_1_out, InstrMem_ctrl[0], not_1_out);
  // SRAM sram_1: pin names not known; wires that end beside it: {1'b1, Program_Counter}, InstrMem_input, and_1_out, clk, 1'b0, 1'b0, 1'b1, sram_1_p8
  not not_2 (not_2_out, and_1_out);
  and and_2 (IR_ctrl[0], Inst_Fetch, not_2_out);
  Control_Unit control_unit_1 (
    .clk(clk), .Write_Back(Write_Back), .Inst_Exec(Inst_Exec), .Inst_Decode(Inst_Decode),
    .Inst_Fetch(Inst_Fetch));
  IR8 ir8_1 (.D_IN_0(sram_1_p8), .D_IN_1({8{1'b0}}), .SRC(1'b0), .CLK(clk), .LD(IR_ctrl[0]), .IR(IR_output));
  Multiplexer #(.Selector_Bits(2), .Bits(8)) multiplexer_1 (
    .sel(IR_output[4:3]), .in_0(8'h1), .in_1(8'h4), .in_2(8'h10), .in_3(8'h40), .out(multiplexer_1_out));
  Multiplexer #(.Bits(8)) multiplexer_2 (
    .sel(Write_Back), .in_0({8{1'b0}}), .in_1(multiplexer_1_out), .out(RegFile_ctrl));
  REGISTER_FILE_4x8_2R1W register_file_4x8_2r1w_1 (
    .RR1(IR_output[4:3]), .RR2(IR_output[2:1]), .WR(IR_output[4:3]),
    .CTRL({RegFile_ctrl[6], RegFile_ctrl[4], RegFile_ctrl[2], RegFile_ctrl[0]}), .clk(clk), .WD(ALU_output),
    .RD1(register_file_4x8_2r1w_1_rd1), .RD2(register_file_4x8_2r1w_1_rd2));  // open: Q1, Q2, Q3, Q4
  Multiplexer #(.Bits(8)) multiplexer_3 (
    .sel(IR_output[0]), .in_0(register_file_4x8_2r1w_1_rd1), .in_1({{6{1'b0}}, IR_output[2:1]}),
    .out(multiplexer_3_out));
  ALU8 alu8_1 (
    .A(multiplexer_3_out), .B(register_file_4x8_2r1w_1_rd2), .C_in(IR_output[5]), .S_0(IR_output[6]),
    .S_1(IR_output[7]), .D(ALU_output));

  assign IR_ctrl[1] = 1'b0;
endmodule

/* Test case:
# =========================================================
# 8-bit processor test
#
# Signals:
#   clk Program_Counter InstrMem_input InstrMem_ctrl
#   IR_output IR_ctrl Write_Back ALU_output
#
# Instruction format:
#   [ opcode(3) | op1(2) | op2(2) | type(1) ]
#
# opcode = ALU control bits = S1 S0 Cin
#
# ALU control / opcode meanings:
#   000 = A + B                  (ADD)
#   001 = A + B + 1              (ADD with carry)
#   010 = A + B̅                 (SUB with borrow)
#   011 = A + B̅ + 1             (SUB)
#   100 = A                      (TRANSFER A)
#   101 = A + 1                  (INCREMENT A)
#   110 = A - 1                  (DECREMENT A)
#   111 = A                      (TRANSFER A)
#
# Register encoding:
#   00 = R0
#   01 = R1
#   10 = R2
#   11 = R3
#
# Type bit:
#   0 = R-type
#   1 = I-type
#
# Notes:
# - In R-type, op1 is A and destination, op2 selects register B.
# - In I-type, op2 is the 2-bit immediate value.
# - TRANSFER A should be encoded as I-type here, with op2 filled
#   as an immediate field.
# - Registers are assumed to start at 0.
#
# Program:
#   0: INC   R1        ; R1 = 1
#   1: INC   R1        ; R1 = 2
#   2: ADDI  R2, 3     ; R2 = 3
#   3: ADD   R2, R1    ; R2 = 5
#   4: SUB   R2, R1    ; R2 = 3
#   5: SUBB  R2, R1    ; R2 = 0
#   6: INC   R0        ; R0 = 1
#   7: DEC   R0        ; R0 = 0
#   8: TRANSFER A R2   ; I-type, imm=01, R2 stays 0
#   9: TRANSFER A R2   ; I-type, imm=10, R2 stays 0
# =========================================================

clk Program_Counter InstrMem_input InstrMem_ctrl IR_output IR_ctrl Write_Back ALU_output

# ---------------------------------------------------------
# settle
# ---------------------------------------------------------
#repeat(10) C X 0 0 X X X X

# ---------------------------------------------------------
# program instruction memory
# ---------------------------------------------------------

# ---------------------------------------------------------
# addr 0 : 168 = INC R1
#
# 168 = 0xA8 = 10101000
#
# Breakdown:
#   opcode = 101  -> Increment A
#   op1    = 01   -> R1
#   op2    = 00   -> immediate field present but ignored by INC
#   type   = 0    -> R-type
#
# Meaning:
#   R1 <- R1 + 1
# ---------------------------------------------------------
C X 168 1 X X X X
repeat(3) C X 0 0 X X X X

# ---------------------------------------------------------
# addr 1 : 168 = INC R1
#
# Same instruction again
# Meaning:
#   R1 <- R1 + 1
# ---------------------------------------------------------
C X 168 1 X X X X
repeat(3) C X 0 0 X X X X

C X 168 1 X X X X
repeat(3) C X 0 0 X X X X

C X 168 1 X X X X
repeat(3) C X 0 0 X X X X

# ---------------------------------------------------------
# addr 0 : 168 = INC R2
#
# 176 = 0xA8 = 10110000
#
# Breakdown:
#   opcode = 101  -> Increment A
#   op1    = 10   -> R2
#   op2    = 00   -> immediate field present but ignored by INC
#   type   = 0    -> R-type
#
# Meaning:
#   R2 <- R2 + 1
# ---------------------------------------------------------
C X 176 1 X X X X
repeat(3) C X 0 0 X X X X


C X 176 1 X X X X
repeat(3) C X 0 0 X X X X



# ---------------------------------------------------------
# addr 4 : 114 = SUB R1, R2
#
# 108 = 0x6C = 011 01 10 0
#
# Breakdown:
#   opcode = 011  -> Subtract
#   op1    = 01   -> R2
#   op2    = 10   -> R1
#   type   = 0    -> R-type
#
# Meaning:
#   R2 <- R2 - R1
# ---------------------------------------------------------
C X 108 1 X X X X
repeat(3) C X 0 0 X X X X



# ---------------------------------------------------------
# stop programming
# ---------------------------------------------------------
repeat(2) C X 0 0 X X X X

# ---------------------------------------------------------
# run
# ---------------------------------------------------------
# Expected high-level behavior:
#   R1: 0 -> 1 -> 2
#   R2: 0 -> 3 -> 5 -> 3 -> 0 -> 0 -> 0
#   R0: 0 -> 1 -> 0
# ---------------------------------------------------------
repeat(40) C X 0 0 X X X X
*/
