// Digital circuit ALU8.dig as structural Verilog
module ALU8 (
  input  [7:0] A,
  input  [7:0] B,
  input  C_in,
  input  S_0,
  input  S_1,
  output [7:0] D
);

  wire [7:0] multiplexer_1_out, multiplexer_2_out, multiplexer_3_out, not_1_out;

  assign not_1_out = ~B;  // Not not_1, 8 bits wide
  Multiplexer #(.Bits(8)) multiplexer_1 (.sel(S_0), .in_0(B), .in_1(not_1_out), .out(multiplexer_1_out));
  Multiplexer #(.Bits(8)) multiplexer_2 (.sel(S_0), .in_0({8{1'b0}}), .in_1({8{1'b1}}), .out(multiplexer_2_out));
  Multiplexer #(.Bits(8)) multiplexer_3 (
    .sel(S_1), .in_0(multiplexer_1_out), .in_1(multiplexer_2_out), .out(multiplexer_3_out));
  Add #(.Bits(8)) add_1 (.a(A), .b(multiplexer_3_out), .c_i(C_in), .s(D));  // open: c_o
endmodule
