// Digital circuit Control Unit.dig as structural Verilog
module Control_Unit (
  input  clk,
  output Write_Back,
  output Inst_Exec,
  output Inst_Decode,
  output Inst_Fetch
);

  D_FF FF_1 (.D(Inst_Exec), .C(clk), .Q(Write_Back));  // open: nQ
  D_FF FF_2 (.D(Inst_Decode), .C(clk), .Q(Inst_Exec));  // open: nQ
  D_FF FF_3 (.D(Inst_Fetch), .C(clk), .Q(Inst_Decode));  // open: nQ
  D_FF #(.Default(1)) FF_4 (.D(Write_Back), .C(clk), .Q(Inst_Fetch));  // open: nQ
endmodule
