// Digital circuit IR8.dig as structural Verilog
module IR8 (
  input  [7:0] D_IN_0,
  input  CLK,
  input  LD,
  output [7:0] IR
);

  // REG8_CORE reg8_core_1: pin names not known; wires that end beside it: D_IN_0, LD, 1'b0, CLK, IR
endmodule
