// Digital circuit PC8.dig as structural Verilog
module PC8 (
  input  INC,
  input  LD,
  input  [7:0] Val,
  input  RST,
  input  CLK,
  output [7:0] PC
);

  wire or_1_out;
  wire [7:0] add_1_s, reg8_core_1_p1;

  or or_1 (or_1_out, INC, LD);
  // REG8_CORE reg8_core_1: pin names not known; wires that end beside it: reg8_core_1_p1, or_1_out, RST, CLK, PC
  Add #(.Bits(8)) add_1 (.a(PC), .b(8'h1), .c_i(1'b0), .s(add_1_s));  // open: c_o
  Multiplexer #(.Bits(8)) multiplexer_1 (.sel(LD), .in_0(add_1_s), .in_1(Val), .out(reg8_core_1_p1));
endmodule
