// Digital circuit REGISTER_FILE_4x8_2R1W.dig as structural Verilog
module REGISTER_FILE_4x8_2R1W (
  input  [1:0] RR1,
  input  [1:0] RR2,
  input  [1:0] WR,
  input  [3:0] CTRL,
  input  clk,
  input  [7:0] WD,
  output [7:0] RD1,
  output [7:0] RD2,
  output [7:0] Q1,
  output [7:0] Q2,
  output [7:0] Q3,
  output [7:0] Q4
);

  wire and_1_out, and_2_out, and_3_out, and_4_out, decoder_1_out_0, decoder_1_out_1, decoder_1_out_2,
       decoder_1_out_3;

  Decoder #(.Selector_Bits(2)) decoder_1 (
    .sel(WR), .out_0(decoder_1_out_0), .out_1(decoder_1_out_1), .out_2(decoder_1_out_2),
    .out_3(decoder_1_out_3));
  and and_1 (and_1_out, decoder_1_out_0, CTRL[0]);
  and and_2 (and_2_out, decoder_1_out_1, CTRL[1]);
  and and_3 (and_3_out, decoder_1_out_2, CTRL[2]);
  and and_4 (and_4_out, decoder_1_out_3, CTRL[3]);
  // REG8_CORE REG_R0: pin names not known; wires that end beside it: WD, and_1_out, 1'b0, clk, Q1
  // REG8_CORE REG_R1: pin names not known; wires that end beside it: WD, and_2_out, 1'b0, clk, Q2
  // REG8_CORE REG_R2: pin names not known; wires that end beside it: WD, and_3_out, 1'b0, clk, Q3
  // REG8_CORE REG_R3: pin names not known; wires that end beside it: WD, and_4_out, 1'b0, clk, Q4
  Multiplexer #(.Selector_Bits(2), .Bits(8)) multiplexer_1 (
    .sel(RR1), .in_0(Q1), .in_1(Q2), .in_2(Q3), .in_3(Q4), .out(RD1));
  Multiplexer #(.Selector_Bits(2), .Bits(8)) multiplexer_2 (
    .sel(RR2), .in_0(Q1), .in_1(Q2), .in_2(Q3), .in_3(Q4), .out(RD2));
endmodule
