// Digital circuit SRAM.dig as structural Verilog
module SRAM (
  input  [3:0] ADDR,
  input  [7:0] DATA_IN,
  input  STORE,
  input  CLK,
  input  SET,
  output [7:0] DATA
);

  RAMDualPort #(.AddrBits(4), .Bits(8)) ramdualport_1 (
    .A(ADDR), .Din(DATA_IN), .str(STORE), .C(CLK), .ld(SET), .D(DATA));
endmodule

/* Test case:
ADDR DATA_IN STORE CLK SET CLEAR LOAD DATA

# Write 0xA8 to address 0
0 0xA8 1 C 1 0 1 X

# Read back address 0
0 0xA8 0 C 1 0 1 0xA8

# Write 0xB0 to address 1
1 0xB0 1 C 1 0 1 X

# Read back address 1
1 0xB0 0 C 1 0 1 0xB0

# Read address 0 again
0 0 0 C 1 0 1 0xA8
*/
